# Fritzing sketch With toggle (saved by Fritzing 0.9.3b)

parts:
  S1 = Pushbutton [package="[THT]"]
  Деталь2 = Arduino Uno (Rev3) - ICSP
  S2 = Pushbutton [package="[THT]"]
  S3 = Pushbutton [package="[THT]"]
  VCC1 = Battery
  Q1 = LTR-301 [package=ltr-301]
  J1 = Piezo Speaker
  R6 = Resistor [tolerance=±5% resistance=10 package=THT]
  R7 = Resistor [tolerance=±5% resistance=10 package=THT]
  R8 = Resistor [tolerance=±5% resistance=10 package=THT]
  U1 = SD_CARD_SOCKET [package=sdcard_4uconn]
  R9 = Resistor [tolerance=±5% resistance=100 package=THT]
  DS1 = DS18B20 1-Wire Temperature Sensor [part_number=DS18B20]
  X1 = USB Connectors [package=usb-microb]  # not connected
  Деталь3 = Arduino Pro Mini (5V)
  S4 = Toggle Switch [package=THT]
  S5 = Toggle Switch [package=THT]

nets:
  N1: S1.Pin_1, S1.Pin_2, Деталь2.D5_PWM, R8.Pin_0
  N2: Деталь2.D8, DS1.VDD
  N3: Деталь2.D9_PWM, R9.Pin_0
  N4: Деталь2.D10_PWM/SS, J1.pin2
  N5: Деталь2.D11_PWM/MOSI, U1.DAT2
  N6: Деталь2.D12/MISO, U1.DAT0
  N7: Деталь2.D13/SCK, U1.DAT1
  N8: Деталь2.GND, J1.pin1, R6.Pin_1, R7.Pin_1, R8.Pin_1
  N9: Деталь2.D2, S3.Pin_1, S3.Pin_2, R6.Pin_0
  N10: Деталь2.D3_PWM, S2.Pin_1, S2.Pin_2, R7.Pin_0
  N11: Деталь2.D4, U1.CD
  N12: Деталь2.D7, S5.L2
  N13: VCC1.+, Деталь3.GND
  N14: Q1.C, R9.Pin_1
  N15: Деталь3.DTR, S4.COM
